// Logisim project project-logisim.circ as structural Verilog: 14 circuits, main circuit main
module main (
  input  in_1,
  input  in_2,
  input  in_3,
  input  in_4,
  output reset,
  output out_6,
  output out_7,
  output out_8,
  output out_9,
  output out_10
);

  wire ac_control_1_out_4, ac_control_1_out_5, ac_control_1_out_6, ac_control_1_out_7, bcd_to_seven_1_a,
       bcd_to_seven_1_b, bcd_to_seven_1_c, bcd_to_seven_1_d, bcd_to_seven_1_e, bcd_to_seven_1_f,
       bcd_to_seven_1_g, bcd_to_seven_2_a, bcd_to_seven_2_b, bcd_to_seven_2_c, bcd_to_seven_2_d,
       bcd_to_seven_2_e, bcd_to_seven_2_f, bcd_to_seven_2_g, bcd_to_seven_3_a, bcd_to_seven_3_b,
       bcd_to_seven_3_c, bcd_to_seven_3_d, bcd_to_seven_3_e, bcd_to_seven_3_f, bcd_to_seven_3_g,
       bcd_to_seven_4_a, bcd_to_seven_4_b, bcd_to_seven_4_c, bcd_to_seven_4_d, bcd_to_seven_4_e,
       bcd_to_seven_4_f, bcd_to_seven_4_g, button_1_out, button_2_out, button_3_out, button_4_out,
       clock_1_out, modified_counter_1_lsb, modified_counter_1_out_20, modified_counter_1_out_21,
       modified_counter_1_out_22, modified_counter_1_out_25, n8421_to_bcd_1_out_5, n8421_to_bcd_1_out_6,
       n8421_to_bcd_1_out_7, n8421_to_bcd_1_out_8, n8421_to_bcd_1_out_9, n8421_to_bcd_1_out_10,
       n8421_to_bcd_1_out_11, n8421_to_bcd_1_out_12, n8421_to_bcd_2_out_5, n8421_to_bcd_2_out_6,
       n8421_to_bcd_2_out_7, n8421_to_bcd_2_out_8, n8421_to_bcd_2_out_9, n8421_to_bcd_2_out_10,
       n8421_to_bcd_2_out_11, n8421_to_bcd_2_out_12, not_1_out, not_2_out, power_control_1_b0,
       power_control_1_b1, power_control_1_b2, power_control_1_b3;
  wire [2:0] priority_encoder_1_out;

  not not_1 (not_1_out, 1'b1);
  Clock clock_1 (.out(clock_1_out));
  Button button_1 (.out(button_1_out));
  Priority_Encoder priority_encoder_1 (
    .in0(not_1_out), .in1(power_control_1_b3), .in2(power_control_1_b2), .in3(power_control_1_b1),
    .in4(power_control_1_b0), .in5(not_1_out), .in6(not_1_out), .in7(not_1_out),
    .out(priority_encoder_1_out), .en_in(1'b1));  // open: gs, en_out
  electricity_bill electricity_bill_1 (
    .Clock(clock_1_out), .Reset(button_1_out), .in_1(priority_encoder_1_out[2]),
    .in_2(priority_encoder_1_out[1]), .in_3(priority_encoder_1_out[0]), .out_7(reset), .out_8(out_6),
    .out_9(out_7), .out_10(out_8), .out_11(out_9), .out_12(out_10));  // open: out_6
  LED led_1 (.in(power_control_1_b0));
  LED led_2 (.in(power_control_1_b1));
  ac_control ac_control_1 (
    .in_1(power_control_1_b1), .in_2(power_control_1_b2), .in_3(power_control_1_b3),
    .out_4(ac_control_1_out_4), .out_5(ac_control_1_out_5), .out_6(ac_control_1_out_6),
    .out_7(ac_control_1_out_7));
  LED led_3 (.in(ac_control_1_out_5));
  LED led_4 (.in(ac_control_1_out_4));
  LED led_5 (.in(modified_counter_1_out_25));
  power_control power_control_1 (
    .B3(power_control_1_b3), .B2(power_control_1_b2), .B1(power_control_1_b1), .B0(power_control_1_b0),
    .in_1(in_1), .Max_value(in_2), .in_3(in_3), .in_4(in_4), .in_5(modified_counter_1_out_20),
    .in_6(modified_counter_1_out_21), .in_7(modified_counter_1_out_22), .in_8(modified_counter_1_lsb));
  LED led_6 (.in(ac_control_1_out_7));
  LED led_7 (.in(ac_control_1_out_6));
  Button button_2 (.out(button_2_out));
  Button button_3 (.out(button_3_out));
  LED led_8 (.in(power_control_1_b2));
  LED led_9 (.in(power_control_1_b3));
  BCD_to_seven bcd_to_seven_1 (
    .A3(n8421_to_bcd_1_out_5), .A2(n8421_to_bcd_1_out_6), .A1(n8421_to_bcd_1_out_7),
    .A0(n8421_to_bcd_1_out_8), .a(bcd_to_seven_1_a), .b(bcd_to_seven_1_b), .c(bcd_to_seven_1_c),
    .d(bcd_to_seven_1_d), .e(bcd_to_seven_1_e), .f(bcd_to_seven_1_f), .g(bcd_to_seven_1_g));
  _7_Segment_Display u_7_segment_display_1 (
    .g(bcd_to_seven_1_g), .f(bcd_to_seven_1_f), .a(bcd_to_seven_1_a), .b(bcd_to_seven_1_b),
    .e(bcd_to_seven_1_e), .d(bcd_to_seven_1_d), .c(bcd_to_seven_1_c));  // open: dp
  not not_2 (not_2_out, 1'b1);
  modified_counter modified_counter_1 (
    .Up_count(button_3_out), .Down_count(button_2_out), .in_1(not_2_out), .in_2(not_2_out), .in_3(not_2_out),
    .in_4(not_2_out), .in_5(not_2_out), .in_6(not_2_out), .in_7(in_1), .in_8(in_2), .in_9(in_3),
    .in_10(in_4), .out_25(modified_counter_1_out_25), .out_20(modified_counter_1_out_20),
    .out_21(modified_counter_1_out_21), .out_22(modified_counter_1_out_22), .LSB(modified_counter_1_lsb),
    .Reset(button_4_out));  // open: MSB, out_15, out_16, out_17, out_18, out_19, out_24
  _8421_to_BCD u_8421_to_bcd_1 (
    .in_1(modified_counter_1_out_20), .in_2(modified_counter_1_out_21), .in_3(modified_counter_1_out_22),
    .in_4(modified_counter_1_lsb), .out_5(n8421_to_bcd_1_out_5), .out_6(n8421_to_bcd_1_out_6),
    .out_7(n8421_to_bcd_1_out_7), .out_8(n8421_to_bcd_1_out_8), .out_9(n8421_to_bcd_1_out_9),
    .out_10(n8421_to_bcd_1_out_10), .out_11(n8421_to_bcd_1_out_11), .out_12(n8421_to_bcd_1_out_12));
  Button button_4 (.out(button_4_out));
  BCD_to_seven bcd_to_seven_2 (
    .A3(n8421_to_bcd_1_out_9), .A2(n8421_to_bcd_1_out_10), .A1(n8421_to_bcd_1_out_11),
    .A0(n8421_to_bcd_1_out_12), .a(bcd_to_seven_2_a), .b(bcd_to_seven_2_b), .c(bcd_to_seven_2_c),
    .d(bcd_to_seven_2_d), .e(bcd_to_seven_2_e), .f(bcd_to_seven_2_f), .g(bcd_to_seven_2_g));
  _7_Segment_Display u_7_segment_display_2 (
    .g(bcd_to_seven_2_g), .f(bcd_to_seven_2_f), .a(bcd_to_seven_2_a), .b(bcd_to_seven_2_b),
    .e(bcd_to_seven_2_e), .d(bcd_to_seven_2_d), .c(bcd_to_seven_2_c));  // open: dp
  BCD_to_seven bcd_to_seven_3 (
    .A3(n8421_to_bcd_2_out_5), .A2(n8421_to_bcd_2_out_6), .A1(n8421_to_bcd_2_out_7),
    .A0(n8421_to_bcd_2_out_8), .a(bcd_to_seven_3_a), .b(bcd_to_seven_3_b), .c(bcd_to_seven_3_c),
    .d(bcd_to_seven_3_d), .e(bcd_to_seven_3_e), .f(bcd_to_seven_3_f), .g(bcd_to_seven_3_g));
  _7_Segment_Display u_7_segment_display_3 (
    .g(bcd_to_seven_3_g), .f(bcd_to_seven_3_f), .a(bcd_to_seven_3_a), .b(bcd_to_seven_3_b),
    .e(bcd_to_seven_3_e), .d(bcd_to_seven_3_d), .c(bcd_to_seven_3_c));  // open: dp
  _8421_to_BCD u_8421_to_bcd_2 (
    .in_1(in_1), .in_2(in_2), .in_3(in_3), .in_4(in_4), .out_5(n8421_to_bcd_2_out_5),
    .out_6(n8421_to_bcd_2_out_6), .out_7(n8421_to_bcd_2_out_7), .out_8(n8421_to_bcd_2_out_8),
    .out_9(n8421_to_bcd_2_out_9), .out_10(n8421_to_bcd_2_out_10), .out_11(n8421_to_bcd_2_out_11),
    .out_12(n8421_to_bcd_2_out_12));
  BCD_to_seven bcd_to_seven_4 (
    .A3(n8421_to_bcd_2_out_9), .A2(n8421_to_bcd_2_out_10), .A1(n8421_to_bcd_2_out_11),
    .A0(n8421_to_bcd_2_out_12), .a(bcd_to_seven_4_a), .b(bcd_to_seven_4_b), .c(bcd_to_seven_4_c),
    .d(bcd_to_seven_4_d), .e(bcd_to_seven_4_e), .f(bcd_to_seven_4_f), .g(bcd_to_seven_4_g));
  _7_Segment_Display u_7_segment_display_4 (
    .g(bcd_to_seven_4_g), .f(bcd_to_seven_4_f), .a(bcd_to_seven_4_a), .b(bcd_to_seven_4_b),
    .e(bcd_to_seven_4_e), .d(bcd_to_seven_4_d), .c(bcd_to_seven_4_c));  // open: dp

  // Notes on the sheet:
  //   |
  //   |
  //   |
  //   |
  //   |
  //   |
  //   |
  //   |
  //   |
  //   |
  //   |
  //   |
  //   |
  //   |
  //   |
  //   |
  //   Current bill
  //   LED (POWER)
  //   LED (POWER)
  //   Entry door
  //   Temp
  //   EXIT
  //   ENTRY
  //   DOOR
  //   -----------------------------------------------------------------------------------
  //   *** ROOM ***
  //   LED (POWER)
  //   AC power
  //   LED (POWER)
  //   -----------------------------------------
  //   Entry and
  //   AUTOMATIC VISITOR COUNTER AND POWER CONTROL 
  //   |
  //   |
  //   |
  //   |
  //   |
  //   |
  //   |
  //   |
  //   |
  //   |
  //   |
  //   |
  //   |
  //   |
  //   |
  //   |
  //   |
  //   Exit pulse controlled using laser detectors
  //   BCD to
  //   7-segment
  //   Counter
  //   Binary to BCD
  //   Input maximum limit
  //   Reset
  //   BCD to
  //   7-segment
  //   COUNT
  //   BCD to
  //   7-segment
  //   Binary to BCD
  //   BCD to
  //   7-segment
endmodule

module Mux (
  input  Input_1,
  input  Input_2,
  input  Select_bit,
  output out_4
);

  wire and_1_out, and_2_out, not_1_out;

  not not_1 (not_1_out, Select_bit);
  and and_1 (and_1_out, not_1_out, Input_1);
  and and_2 (and_2_out, Select_bit, Input_2);
  or or_1 (out_4, and_1_out, and_2_out);

  // Notes on the sheet:
  //   2 to 1 Multiplexer
endmodule

module SR_Latch (
  input  S,
  input  R,
  output Q,
  output Q_prime
);

  nor nor_1 (Q, R, Q_prime);
  nor nor_2 (Q_prime, Q, S);

  // Notes on the sheet:
  //   SR Latch
endmodule

module synchronous_counter (
  input  Toggle,
  input  Up_count,
  input  Down_count,
  input  Reset,
  output MSB,
  output out_6,
  output out_7,
  output out_8,
  output out_9,
  output out_10,
  output out_11,
  output out_12,
  output out_13,
  output LSB
);

  wire and_1_out, and_2_out, and_3_out, and_4_out, and_5_out, and_6_out, and_7_out, and_8_out, and_9_out,
       and_10_out, and_11_out, and_12_out, and_13_out, and_14_out, and_15_out, and_16_out, and_17_out,
       and_18_out, j_k_ff_1_qn, j_k_ff_2_qn, j_k_ff_3_qn, j_k_ff_4_qn, j_k_ff_5_qn, j_k_ff_6_qn, j_k_ff_7_qn,
       j_k_ff_8_qn, j_k_ff_9_qn, not_1_out, not_2_out, or_1_out, or_2_out, or_3_out, or_4_out, or_5_out,
       or_6_out, or_7_out, or_8_out, or_9_out, or_10_out, sr_latch_1_q;

  SR_Latch sr_latch_1 (.S(Up_count), .R(Down_count), .Q(sr_latch_1_q));  // open: Q_prime
  or or_1 (or_1_out, Down_count, Up_count);
  not not_1 (not_1_out, or_1_out);
  J_K_Flip_Flop j_k_ff_1 (
    .J(Toggle), .clk(not_1_out), .K(Toggle), .Q(LSB), .Qn(j_k_ff_1_qn), .reset(Reset));  // open: preset, en
  not not_2 (not_2_out, sr_latch_1_q);
  and and_1 (and_1_out, sr_latch_1_q, LSB);
  and and_2 (and_2_out, j_k_ff_1_qn, not_2_out);
  or or_2 (or_2_out, and_1_out, and_2_out);
  J_K_Flip_Flop j_k_ff_2 (
    .J(or_2_out), .clk(not_1_out), .K(or_2_out), .Q(out_13), .Qn(j_k_ff_2_qn), .reset(Reset));  // open: preset, en
  and and_3 (and_3_out, and_1_out, out_13);
  and and_4 (and_4_out, j_k_ff_2_qn, and_2_out);
  or or_3 (or_3_out, and_3_out, and_4_out);
  and and_5 (and_5_out, and_3_out, out_12);
  J_K_Flip_Flop j_k_ff_3 (
    .J(or_3_out), .clk(not_1_out), .K(or_3_out), .Q(out_12), .Qn(j_k_ff_3_qn), .reset(Reset));  // open: preset, en
  and and_6 (and_6_out, j_k_ff_3_qn, and_4_out);
  or or_4 (or_4_out, and_5_out, and_6_out);
  J_K_Flip_Flop j_k_ff_4 (
    .J(or_4_out), .clk(not_1_out), .K(or_4_out), .Q(out_11), .Qn(j_k_ff_4_qn), .reset(Reset));  // open: preset, en
  and and_7 (and_7_out, and_5_out, out_11);
  and and_8 (and_8_out, j_k_ff_4_qn, and_6_out);
  or or_5 (or_5_out, and_7_out, and_8_out);
  J_K_Flip_Flop j_k_ff_5 (
    .J(or_5_out), .clk(not_1_out), .K(or_5_out), .Q(out_10), .Qn(j_k_ff_5_qn), .reset(Reset));  // open: preset, en
  and and_9 (and_9_out, and_7_out, out_10);
  and and_10 (and_10_out, j_k_ff_5_qn, and_8_out);
  or or_6 (or_6_out, and_9_out, and_10_out);
  J_K_Flip_Flop j_k_ff_6 (
    .J(or_6_out), .clk(not_1_out), .K(or_6_out), .Q(out_9), .Qn(j_k_ff_6_qn), .reset(Reset));  // open: preset, en
  and and_11 (and_11_out, and_9_out, out_9);
  and and_12 (and_12_out, j_k_ff_6_qn, and_10_out);
  or or_7 (or_7_out, and_11_out, and_12_out);
  J_K_Flip_Flop j_k_ff_7 (
    .J(or_7_out), .clk(not_1_out), .K(or_7_out), .Q(out_8), .Qn(j_k_ff_7_qn), .reset(Reset));  // open: preset, en
  and and_13 (and_13_out, and_11_out, out_8);
  and and_14 (and_14_out, j_k_ff_7_qn, and_12_out);
  or or_8 (or_8_out, and_13_out, and_14_out);
  J_K_Flip_Flop j_k_ff_8 (
    .J(or_8_out), .clk(not_1_out), .K(or_8_out), .Q(out_7), .Qn(j_k_ff_8_qn), .reset(Reset));  // open: preset, en
  and and_15 (and_15_out, and_13_out, out_7);
  and and_16 (and_16_out, j_k_ff_8_qn, and_14_out);
  or or_9 (or_9_out, and_15_out, and_16_out);
  J_K_Flip_Flop j_k_ff_9 (
    .J(or_9_out), .clk(not_1_out), .K(or_9_out), .Q(out_6), .Qn(j_k_ff_9_qn), .reset(Reset));  // open: preset, en
  and and_17 (and_17_out, and_15_out, out_6);
  and and_18 (and_18_out, j_k_ff_9_qn, and_16_out);
  or or_10 (or_10_out, and_17_out, and_18_out);
  J_K_Flip_Flop j_k_ff_10 (
    .J(or_10_out), .clk(not_1_out), .K(or_10_out), .Q(MSB), .reset(Reset));  // open: Qn, preset, en

  // Notes on the sheet:
  //   SR Latch
  //   Clock
  //   10 bit synchronous up/down counter 
  //   COUNT
endmodule

module modified_counter (
  input  in_1,
  input  in_2,
  input  in_3,
  input  in_4,
  input  in_5,
  input  in_6,
  input  in_7,
  input  in_8,
  input  in_9,
  input  in_10,
  input  Up_count,
  input  Reset,
  input  Down_count,
  output MSB,
  output out_15,
  output out_16,
  output out_17,
  output out_18,
  output out_19,
  output out_20,
  output out_21,
  output out_22,
  output LSB,
  output out_24,
  output out_25
);

  wire and_1_out, Mux_2_out_4, mux_3_out_4, mux_4_out_4, mux_5_out_4, mux_6_out_4, mux_7_out_4, mux_8_out_4,
       mux_9_out_4, mux_10_out_4, mux_11_out_4, mux_12_out_4, Mux_out_4, nor_1_out, not_2_out, not_3_out,
       not_5_out, not_6_out, not_7_out, not_8_out, not_9_out, not_10_out, not_11_out, not_12_out, not_13_out,
       not_14_out;

  not not_1 (out_25, and_1_out);
  Mux Mux (.Input_1(Down_count), .Input_2(not_2_out), .Select_bit(nor_1_out), .out_4(Mux_out_4));
  not not_2 (not_2_out, 1'b1);
  not not_3 (not_3_out, 1'b1);
  not not_4 (out_24, nor_1_out);
  Mux Mux_2 (.Input_1(Up_count), .Input_2(not_3_out), .Select_bit(and_1_out), .out_4(Mux_2_out_4));
  nor nor_1 (nor_1_out, MSB, out_15, out_16, out_17, out_18, out_19, out_20, out_21, out_22, LSB);
  synchronous_counter synchronous_counter_1 (
    .Up_count(Mux_2_out_4), .Down_count(Mux_out_4), .Toggle(1'b1), .MSB(MSB), .out_6(out_15), .out_7(out_16),
    .out_8(out_17), .out_9(out_18), .out_10(out_19), .out_11(out_20), .out_12(out_21), .out_13(out_22),
    .LSB(LSB), .Reset(Reset));
  not not_5 (not_5_out, MSB);
  not not_6 (not_6_out, out_15);
  Mux mux_3 (.Input_1(not_6_out), .Input_2(out_15), .Select_bit(in_2), .out_4(mux_3_out_4));
  Mux mux_4 (.Input_1(not_5_out), .Input_2(MSB), .Select_bit(in_1), .out_4(mux_4_out_4));
  not not_7 (not_7_out, out_16);
  Mux mux_5 (.Input_1(not_7_out), .Input_2(out_16), .Select_bit(in_3), .out_4(mux_5_out_4));
  not not_8 (not_8_out, out_17);
  not not_9 (not_9_out, out_18);
  Mux mux_6 (.Input_1(not_8_out), .Input_2(out_17), .Select_bit(in_4), .out_4(mux_6_out_4));
  Mux mux_7 (.Input_1(not_9_out), .Input_2(out_18), .Select_bit(in_5), .out_4(mux_7_out_4));
  not not_10 (not_10_out, out_20);
  not not_11 (not_11_out, out_19);
  Mux mux_8 (.Input_1(not_11_out), .Input_2(out_19), .Select_bit(in_6), .out_4(mux_8_out_4));
  Mux mux_9 (.Input_1(not_10_out), .Input_2(out_20), .Select_bit(in_7), .out_4(mux_9_out_4));
  and and_1 (and_1_out, mux_4_out_4, mux_3_out_4, mux_5_out_4, mux_6_out_4, mux_7_out_4, mux_8_out_4, mux_9_out_4, mux_10_out_4, mux_11_out_4, mux_12_out_4);
  not not_12 (not_12_out, out_21);
  Mux mux_10 (.Input_1(not_12_out), .Input_2(out_21), .Select_bit(in_8), .out_4(mux_10_out_4));
  not not_13 (not_13_out, LSB);
  not not_14 (not_14_out, out_22);
  Mux mux_11 (.Input_1(not_14_out), .Input_2(out_22), .Select_bit(in_9), .out_4(mux_11_out_4));
  Mux mux_12 (.Input_1(not_13_out), .Input_2(LSB), .Select_bit(in_10), .out_4(mux_12_out_4));

  // Notes on the sheet:
  //   Entry door control
  //   Visitor counter
  //   Check underflow
  //   Toggle
  //   Counter IC
  //   COUNT
  //   Check light on/off
  //   Set Max Value
  //   Check overflow
endmodule

module _1_bit_full_adder (
  input  A,
  input  B,
  input  Cin,
  output Sum,
  output Carry
);

  wire and_1_out, and_2_out, xor_1_out;

  xor xor_1 (xor_1_out, A, B);
  xor xor_2 (Sum, xor_1_out, Cin);
  and and_1 (and_1_out, xor_1_out, Cin);
  and and_2 (and_2_out, A, B);
  or or_1 (Carry, and_1_out, and_2_out);
endmodule

module _4_bit_full_adder (
  input  in_1,
  input  B,
  input  in_3,
  input  in_4,
  input  Cin,
  input  in_6,
  input  A,
  input  in_8,
  input  in_9,
  output Cout,
  output out_11,
  output Sum,
  output out_13,
  output out_14
);

  wire n1_bit_full_adder_1_carry, n1_bit_full_adder_2_carry, n1_bit_full_adder_3_carry;

  _1_bit_full_adder u_1_bit_full_adder_1 (
    .A(in_9), .B(in_4), .Cin(Cin), .Sum(out_14), .Carry(n1_bit_full_adder_1_carry));
  _1_bit_full_adder u_1_bit_full_adder_2 (
    .A(in_8), .B(in_3), .Cin(n1_bit_full_adder_1_carry), .Sum(out_13), .Carry(n1_bit_full_adder_2_carry));
  _1_bit_full_adder u_1_bit_full_adder_3 (
    .A(A), .B(B), .Cin(n1_bit_full_adder_2_carry), .Sum(Sum), .Carry(n1_bit_full_adder_3_carry));
  _1_bit_full_adder u_1_bit_full_adder_4 (
    .A(in_6), .B(in_1), .Cin(n1_bit_full_adder_3_carry), .Sum(out_11), .Carry(Cout));
endmodule

module BCD_to_seven (
  input  A3,
  input  A2,
  input  A1,
  input  A0,
  output a,
  output b,
  output c,
  output d,
  output e,
  output f,
  output g
);

  wire and_1_out, and_2_out, and_3_out, and_4_out, and_5_out, and_6_out, and_7_out, and_8_out, and_9_out,
       not_1_out, not_2_out, not_3_out, not_4_out;

  not not_1 (not_1_out, A3);
  not not_2 (not_2_out, A2);
  not not_3 (not_3_out, A1);
  not not_4 (not_4_out, A0);
  and and_1 (and_1_out, A2, A0);
  and and_2 (and_2_out, not_2_out, not_4_out);
  and and_3 (and_3_out, A1, A0);
  and and_4 (and_4_out, not_3_out, not_4_out);
  or or_1 (c, A2, not_3_out, A0);
  and and_5 (and_5_out, A1, not_4_out);
  and and_6 (and_6_out, not_2_out, A1);
  and and_7 (and_7_out, A2, not_3_out);
  and and_8 (and_8_out, A2, not_4_out);
  and and_9 (and_9_out, A0, and_7_out);
  or or_2 (a, and_1_out, and_2_out, A3, A1);
  or or_3 (d, A3, and_2_out, and_5_out, and_6_out, and_9_out);
  or or_4 (b, and_3_out, and_4_out, not_2_out);
  or or_5 (e, and_2_out, and_5_out);
  or or_6 (f, and_4_out, and_7_out, A3, and_8_out);
  or or_7 (g, and_5_out, and_6_out, A3, and_7_out);
endmodule

module _8421_to_BCD (
  input  in_1,
  input  in_2,
  input  in_3,
  input  in_4,
  output out_5,
  output out_6,
  output out_7,
  output out_8,
  output out_9,
  output out_10,
  output out_11,
  output out_12
);

  wire and_1_out, and_2_out, not_2_out, or_1_out;

  not not_1 (out_5, 1'b1);
  or or_1 (or_1_out, and_1_out, and_2_out);
  and and_1 (and_1_out, in_1, in_2);
  and and_2 (and_2_out, in_1, in_3);
  not not_2 (not_2_out, 1'b1);
  _4_bit_full_adder u_4_bit_full_adder_1 (
    .Cin(not_2_out), .in_6(not_2_out), .A(or_1_out), .in_8(or_1_out), .in_9(not_2_out), .in_1(in_1),
    .B(in_2), .in_3(in_3), .in_4(in_4), .Cout(out_8), .out_11(out_9), .Sum(out_10), .out_13(out_11),
    .out_14(out_12));

  assign out_6 = out_5;
  assign out_7 = out_5;

  // Notes on the sheet:
  //   4 BIT binary to BCD 
endmodule

module power_control (
  input  in_1,
  input  Max_value,
  input  in_3,
  input  in_4,
  input  in_5,
  input  in_6,
  input  in_7,
  input  in_8,
  output B3,
  output B2,
  output B1,
  output B0
);

  wire comparator_1_eq;
  wire [3:0] divider_1_out, divider_2_out, multiplier_1_out;

  Divider #(.width(4)) divider_1 (
    .a({in_1, Max_value, in_3, in_4}), .b(4'b0100), .out(divider_1_out));  // open: upper, rem
  Divider #(.width(4)) divider_2 (
    .a({in_1, Max_value, in_3, in_4}), .b(4'b0010), .out(divider_2_out));  // open: upper, rem
  Multiplier #(.width(4)) multiplier_1 (.a(divider_1_out), .b(4'b0011), .out(multiplier_1_out));  // open: cin, cout
  Comparator #(.width(4), .mode("unsigned")) comparator_1 (
    .a({in_5, in_6, in_7, in_8}), .b(4'b0000), .eq(comparator_1_eq));  // open: gt, lt
  Comparator #(.width(4), .mode("unsigned")) comparator_2 (
    .a({in_5, in_6, in_7, in_8}), .b(divider_1_out), .gt(B2));  // open: eq, lt
  Comparator #(.width(4), .mode("unsigned")) comparator_3 (
    .a({in_5, in_6, in_7, in_8}), .b(divider_2_out), .gt(B1));  // open: eq, lt
  Comparator #(.width(4), .mode("unsigned")) comparator_4 (
    .a({in_5, in_6, in_7, in_8}), .b(multiplier_1_out), .gt(B0));  // open: eq, lt
  not not_1 (B3, comparator_1_eq);

  // Notes on the sheet:
  //   Curr value
endmodule

module ac_control (
  input  in_1,
  input  in_2,
  input  in_3,
  output out_4,
  output out_5,
  output out_6,
  output out_7
);

  wire not_1_out, not_2_out;

  not not_1 (not_1_out, in_1);
  and and_1 (out_5, not_1_out, in_3);
  not not_2 (not_2_out, in_2);
  and and_2 (out_4, not_2_out, in_3);

  assign out_6 = in_3;
  assign out_7 = in_3;
endmodule

module _7bitadder (
  input  in_1,
  input  in_2,
  input  in_3,
  input  A3,
  input  A2,
  input  A1,
  input  A0,
  input  in_8,
  input  in_9,
  input  in_10,
  input  B3,
  input  B2,
  input  B1,
  input  B0,
  output out_15,
  output out_16,
  output out_17,
  output out_18,
  output out_19,
  output out_20,
  output out_21,
  output out_22
);

  wire n1bit_new_2_c_2, n1bit_new_3_c_2, n1bit_new_4_c_2, n1bit_new_5_c_2, n1bit_new_6_c_2, n1bit_new_7_c_2,
       not_1_out;

  _1bit_new u_1bit_new_1 (.A(in_1), .B(in_8), .C(n1bit_new_2_c_2), .S(out_17), .C_2(out_16));
  _1bit_new u_1bit_new_2 (.A(in_2), .B(in_9), .C(n1bit_new_3_c_2), .S(out_18), .C_2(n1bit_new_2_c_2));
  _1bit_new u_1bit_new_3 (.A(in_3), .B(in_10), .C(n1bit_new_4_c_2), .S(out_19), .C_2(n1bit_new_3_c_2));
  _1bit_new u_1bit_new_4 (.A(A3), .B(B3), .C(n1bit_new_5_c_2), .S(out_20), .C_2(n1bit_new_4_c_2));
  _1bit_new u_1bit_new_5 (.A(A2), .B(B2), .C(n1bit_new_6_c_2), .S(out_21), .C_2(n1bit_new_5_c_2));
  _1bit_new u_1bit_new_6 (.A(A1), .B(B1), .C(n1bit_new_7_c_2), .S(out_22), .C_2(n1bit_new_6_c_2));
  _1bit_new u_1bit_new_7 (.A(A0), .B(B0), .C(not_1_out), .S(out_15), .C_2(n1bit_new_7_c_2));
  not not_1 (not_1_out, 1'b1);

  // Notes on the sheet:
  //   4-bit Adder , CS101-S1-1
  //   C0
  //   (Initial carry)
endmodule

module _1bit_new (
  input  A,
  input  B,
  input  C,
  output S,
  output C_2
);

  wire and_1_out, and_2_out, xor_1_out, xor_2_out;

  and and_1 (and_1_out, A, B);
  xor xor_1 (xor_1_out, A, B);
  and and_2 (and_2_out, xor_1_out, C);
  xor xor_2 (xor_2_out, A, B);
  or or_1 (C_2, and_1_out, and_2_out);
  xor xor_3 (S, xor_2_out, C);
endmodule

module electricity_bill (
  input  in_1,
  input  in_2,
  input  in_3,
  input  Clock,
  input  Reset,
  output out_6,
  output out_7,
  output out_8,
  output out_9,
  output out_10,
  output out_11,
  output out_12
);

  wire n7bitadder_1_out_15, n7bitadder_1_out_16, n7bitadder_1_out_17, n7bitadder_1_out_18,
       n7bitadder_1_out_19, n7bitadder_1_out_20, n7bitadder_1_out_21, n7bitadder_1_out_22, not_1_out;

  D_Flip_Flop d_ff_1 (.clk(Clock), .D(n7bitadder_1_out_17), .Q(out_6), .reset(Reset));  // open: Qn, preset, en
  D_Flip_Flop d_ff_2 (.clk(Clock), .D(n7bitadder_1_out_16), .reset(Reset));  // open: Q, Qn, preset, en
  D_Flip_Flop d_ff_3 (.clk(Clock), .D(n7bitadder_1_out_18), .Q(out_7), .reset(Reset));  // open: Qn, preset, en
  not not_1 (not_1_out, 1'b1);
  _7bitadder u_7bitadder_1 (
    .in_8(out_6), .in_9(out_7), .in_10(out_8), .B3(out_9), .B2(out_10), .B1(out_11), .B0(out_12),
    .in_1(not_1_out), .in_2(not_1_out), .in_3(not_1_out), .A3(not_1_out), .A2(in_1), .A1(in_2), .A0(in_3),
    .out_16(n7bitadder_1_out_16), .out_17(n7bitadder_1_out_17), .out_18(n7bitadder_1_out_18),
    .out_19(n7bitadder_1_out_19), .out_20(n7bitadder_1_out_20), .out_21(n7bitadder_1_out_21),
    .out_22(n7bitadder_1_out_22), .out_15(n7bitadder_1_out_15));
  D_Flip_Flop d_ff_4 (.clk(Clock), .D(n7bitadder_1_out_19), .Q(out_8), .reset(Reset));  // open: Qn, preset, en
  D_Flip_Flop d_ff_5 (.clk(Clock), .D(n7bitadder_1_out_21), .Q(out_10), .reset(Reset));  // open: Qn, preset, en
  D_Flip_Flop d_ff_6 (.clk(Clock), .D(n7bitadder_1_out_20), .Q(out_9), .reset(Reset));  // open: Qn, preset, en
  D_Flip_Flop d_ff_7 (.clk(Clock), .D(n7bitadder_1_out_22), .Q(out_11), .reset(Reset));  // open: Qn, preset, en
  D_Flip_Flop d_ff_8 (.clk(Clock), .D(n7bitadder_1_out_15), .Q(out_12), .reset(Reset));  // open: Qn, preset, en

  // Notes on the sheet:
  //   Num of bulbs
endmodule
